// Logisim project CPU.circ as structural Verilog
module main (
  input  in_1,
  input  in_2,
  input  in_3,
  input  in_4,
  input  Reset,
  input  in_6,
  input  in_7,
  input  in_8,
  input  in_9,
  input  in_10,
  input  in_11,
  input  in_12,
  output [2:0] ALUStatus
);

  wire clock_1_out, clock_2_out, clock_3_out, clock_4_out, clock_5_out, clock_6_out, clock_7_out,
       clock_8_out, clock_9_out, clock_10_out, cu_1_p9, cu_1_p10, cu_1_p12, cu_1_p13, cu_1_p15, cu_1_p16,
       data_registers_1_eq, display_data_1_out_4, display_data_1_out_5, display_data_1_out_6,
       display_data_1_out_7, display_data_1_out_8, display_data_1_out_9, display_data_1_out_10,
       display_data_1_out_11, display_data_1_out_12, display_data_1_out_13, display_data_1_out_14,
       display_data_1_out_15, display_data_1_out_16, display_data_1_out_17, display_data_1_out_18,
       display_data_1_out_19, display_data_1_out_20, display_data_1_out_21, display_data_1_out_22,
       display_data_1_out_23, display_data_1_out_24, not_1_out, not_2_out, ramaddrcount_1_out_2, rw_1_out_4,
       rw_1_writetrigger, shoulddisplay_1_out_3, shoulddisplay_1_out_4;
  wire [2:0] alu_1_status, cu_1_p11;
  wire [3:0] AR_out1, ClkCount, MAR_out1, multiplexer_1_out, pc_incr_1_pcout, PC_out1, pre_bus_1_out_6,
       pre_bus_1_out_6_2;
  wire [7:0] alu_1_aregister, byte_storage_compact_1_dataout, cu_1_p14, cu_1_p17, data_registers_1_data0,
       data_registers_1_data1, data_registers_1_dataoutput, DR_dataout, IR_dataout, MBR_dataout,
       numeric_keypad_1_out_11, ram16c_1_out_23, ram16c_1_out_24, ram16c_1_out_25, ram16c_1_out_26,
       ram16c_1_out_27, ram16c_1_out_28, ram16c_1_out_29, ram16c_1_out_30, ram16c_1_out_31, ram16c_1_out_32,
       ram16c_1_out_33, ram16c_1_out_34, ram16c_1_out_35, ram16c_1_out_36, ram16c_1_out_37, ram16c_1_out_38,
       ram16c_1_out_39, rom_bonus_1_out_1, rom_bonus_1_out_2, rom_bonus_1_out_3, rom_bonus_1_out_4,
       rom_bonus_1_out_5, rom_bonus_1_out_6, rom_bonus_1_out_7, rom_bonus_1_out_8, rom_bonus_1_out_9,
       rom_bonus_1_out_10, rom_bonus_1_out_11, rom_bonus_1_out_12, rom_bonus_1_out_13, rom_bonus_1_out_14,
       rom_bonus_1_out_15, rom_bonus_1_out_16;

  Clock clock_1 (.out(clock_1_out));
  // delay_base delay_base_1: pin names not known; wires that end beside it: clock_1_out, Reset, ClkCount
  // Probe on ClkCount
  RW rw_1 (
    .out_4(rw_1_out_4), .WriteTrigger(rw_1_writetrigger), .in_2(ClkCount),
    .in_1({pre_bus_1_out_6_2, pre_bus_1_out_6}));
  // Probe on rw_1_writetrigger
  // Probe on ramaddrcount_1_out_2
  RAMaddrCount ramaddrcount_1 (.out_2(ramaddrcount_1_out_2), .in_1(ClkCount));
  not not_1 (not_1_out, clock_2_out);
  Clock clock_2 (.out(clock_2_out));
  four_bit_storage AR (.Out1(AR_out1), .Write(ramaddrcount_1_out_2), .Clock(not_1_out), .In1(pre_bus_1_out_6));
  // Probe on AR_out1
  Clock clock_3 (.out(clock_3_out));
  ROM_bonus rom_bonus_1 (
    .out_1(rom_bonus_1_out_1), .out_2(rom_bonus_1_out_2), .out_3(rom_bonus_1_out_3),
    .out_4(rom_bonus_1_out_4), .out_5(rom_bonus_1_out_5), .out_6(rom_bonus_1_out_6),
    .out_7(rom_bonus_1_out_7), .out_8(rom_bonus_1_out_8), .out_9(rom_bonus_1_out_9),
    .out_10(rom_bonus_1_out_10), .out_11(rom_bonus_1_out_11), .out_12(rom_bonus_1_out_12),
    .out_13(rom_bonus_1_out_13), .out_14(rom_bonus_1_out_14), .out_15(rom_bonus_1_out_15),
    .out_16(rom_bonus_1_out_16));
  RAM16C ram16c_1 (
    .Addr(AR_out1), .EnableWrite(rw_1_out_4), .CLK(clock_3_out),
    .DataInput({pre_bus_1_out_6_2, pre_bus_1_out_6}), .ROMoverwrite(in_12), .Reset(Reset),
    .in_7(rom_bonus_1_out_1), .in_8(rom_bonus_1_out_2), .in_9(rom_bonus_1_out_3), .in_10(rom_bonus_1_out_4),
    .in_11(rom_bonus_1_out_5), .in_12(rom_bonus_1_out_6), .in_13(rom_bonus_1_out_7),
    .in_14(rom_bonus_1_out_8), .in_15(rom_bonus_1_out_9), .in_16(rom_bonus_1_out_10),
    .in_17(rom_bonus_1_out_11), .in_18(rom_bonus_1_out_12), .in_19(rom_bonus_1_out_13),
    .in_20(rom_bonus_1_out_14), .in_21(rom_bonus_1_out_15), .in_22(rom_bonus_1_out_16),
    .out_23(ram16c_1_out_23), .out_24(ram16c_1_out_24), .out_25(ram16c_1_out_25), .out_26(ram16c_1_out_26),
    .out_27(ram16c_1_out_27), .out_28(ram16c_1_out_28), .out_29(ram16c_1_out_29), .out_30(ram16c_1_out_30),
    .out_31(ram16c_1_out_31), .out_32(ram16c_1_out_32), .out_33(ram16c_1_out_33), .out_34(ram16c_1_out_34),
    .out_35(ram16c_1_out_35), .out_36(ram16c_1_out_36), .out_37(ram16c_1_out_37), .out_38(ram16c_1_out_38),
    .out_39(ram16c_1_out_39));
  // Probe on ram16c_1_out_24
  // Probe on ram16c_1_out_25
  // Probe on ram16c_1_out_26
  // Probe on ram16c_1_out_27
  // Probe on ram16c_1_out_28
  // Probe on ram16c_1_out_29
  // Probe on ram16c_1_out_30
  // Probe on ram16c_1_out_31
  // Probe on ram16c_1_out_32
  // Probe on ram16c_1_out_33
  // Probe on ram16c_1_out_34
  // Probe on ram16c_1_out_35
  // Probe on ram16c_1_out_36
  // Probe on ram16c_1_out_37
  // Probe on ram16c_1_out_38
  // Probe on ram16c_1_out_39
  numeric_keypad numeric_keypad_1 (
    .D0(in_1), .D1(in_2), .D2(in_3), .D3(in_4), .D4(in_6), .D5(in_7), .D6(in_8), .D7(in_9), .D8(in_10),
    .D9(in_11), .out_11(numeric_keypad_1_out_11));
  // Probe on ram16c_1_out_23
  // Probe on numeric_keypad_1_out_11
  Clock clock_4 (.out(clock_4_out));
  byte_storage_compact DR (.datain(ram16c_1_out_23), .dataout(DR_dataout), .EnableWrite(1'b1), .Clock(clock_4_out));
  // Probe on {pre_bus_1_out_6_2, pre_bus_1_out_6}
  // Probe on shoulddisplay_1_out_3
  pre_bus pre_bus_1 (
    .CPU(cu_1_p14), .RAM(DR_dataout), .PC(MAR_out1), .out_6({pre_bus_1_out_6_2, pre_bus_1_out_6}),
    .Count(ClkCount), .Keypad(numeric_keypad_1_out_11));
  // Probe on cu_1_p17
  Clock clock_5 (.out(clock_5_out));
  ShouldDisplay shoulddisplay_1 (
    .in_1({pre_bus_1_out_6_2, pre_bus_1_out_6}), .out_3(shoulddisplay_1_out_3), .in_2(ClkCount),
    .out_4(shoulddisplay_1_out_4));
  Clock clock_6 (.out(clock_6_out));
  not not_2 (not_2_out, clock_5_out);
  byte_storage_compact byte_storage_compact_1 (
    .datain({pre_bus_1_out_6_2, pre_bus_1_out_6}), .dataout(byte_storage_compact_1_dataout),
    .EnableWrite(shoulddisplay_1_out_4), .Clock(not_2_out));
  // Probe on cu_1_p14
  _7_Segment_Display u_7_segment_display_1 (
    .g(display_data_1_out_11), .f(display_data_1_out_12), .a(display_data_1_out_13),
    .b(display_data_1_out_14), .e(display_data_1_out_15), .d(display_data_1_out_16), .c(display_data_1_out_17));  // open: dp
  _7_Segment_Display u_7_segment_display_2 (
    .g(display_data_1_out_4), .f(display_data_1_out_5), .a(display_data_1_out_6), .b(display_data_1_out_7),
    .e(display_data_1_out_8), .d(display_data_1_out_9), .c(display_data_1_out_10));  // open: dp
  // Probe on data_registers_1_data0
  // Probe on data_registers_1_data1
  data_registers data_registers_1 (
    .Clk(clock_6_out), .Rw(cu_1_p12), .Which(cu_1_p9), .DataInput(cu_1_p17),
    .DataOutput(data_registers_1_dataoutput), .Data0(data_registers_1_data0), .Data1(data_registers_1_data1),
    .Eq(data_registers_1_eq));
  _7_Segment_Display u_7_segment_display_3 (
    .g(display_data_1_out_18), .f(display_data_1_out_19), .a(display_data_1_out_20),
    .b(display_data_1_out_21), .e(display_data_1_out_22), .d(display_data_1_out_23), .c(display_data_1_out_24));  // open: dp
  display_data display_data_1 (
    .out_17(display_data_1_out_17), .out_16(display_data_1_out_16), .out_15(display_data_1_out_15),
    .out_14(display_data_1_out_14), .out_13(display_data_1_out_13), .out_12(display_data_1_out_12),
    .out_11(display_data_1_out_11), .out_10(display_data_1_out_10), .out_9(display_data_1_out_9),
    .out_8(display_data_1_out_8), .out_7(display_data_1_out_7), .out_6(display_data_1_out_6),
    .out_5(display_data_1_out_5), .out_4(display_data_1_out_4), .Reset(Reset),
    .in_1(byte_storage_compact_1_dataout), .out_18(display_data_1_out_18), .out_19(display_data_1_out_19),
    .out_20(display_data_1_out_20), .out_21(display_data_1_out_21), .out_22(display_data_1_out_22),
    .out_23(display_data_1_out_23), .out_24(display_data_1_out_24));  // open: Error
  // Probe on data_registers_1_data0
  // Probe on data_registers_1_data1
  // Probe on MAR_out1
  ALU alu_1 (
    .Status(alu_1_status), .in_3(data_registers_1_data1), .ARegister(alu_1_aregister),
    .Enable_Mult_AddSub(cu_1_p11), .in_2(data_registers_1_data0));
  Clock clock_7 (.out(clock_7_out));
  four_bit_storage MAR (.Out1(MAR_out1), .Write(clock_7_out), .Clock(1'b1), .In1(PC_out1));
  // Probe on MBR_dataout
  Clock clock_8 (.out(clock_8_out));
  byte_storage_compact MBR (
    .datain({pre_bus_1_out_6_2, pre_bus_1_out_6}), .dataout(MBR_dataout), .EnableWrite(cu_1_p13),
    .Clock(clock_8_out));
  // Probe on alu_1_aregister
  // Probe on PC_out1
  Clock clock_9 (.out(clock_9_out));
  four_bit_storage PC (.Out1(PC_out1), .Write(clock_9_out), .Clock(1'b1), .In1(multiplexer_1_out));
  // Probe on IR_dataout
  Clock clock_10 (.out(clock_10_out));
  byte_storage_compact IR (.datain(MBR_dataout), .dataout(IR_dataout), .EnableWrite(cu_1_p15), .Clock(clock_10_out));
  // CU cu_1: pin names not known; wires that end beside it: IR_dataout, MBR_dataout, ClkCount, data_registers_1_eq, alu_1_aregister, alu_1_status, data_registers_1_dataoutput, ALUStatus, cu_1_p9, cu_1_p10, cu_1_p11, cu_1_p12, cu_1_p13, cu_1_p14, cu_1_p15, cu_1_p16, cu_1_p17
  PC_incr pc_incr_1 (.StopIn(cu_1_p10), .Counter(ClkCount), .PCIn(PC_out1), .PCOut(pc_incr_1_pcout));
  Multiplexer #(.width(4), .enable("false")) multiplexer_1 (
    .in0(pc_incr_1_pcout), .in1(IR_dataout[3:0]), .out(multiplexer_1_out), .sel(cu_1_p16));
endmodule

module ALU (
  input  [2:0] Enable_Mult_AddSub,
  input  [7:0] in_2,
  input  [7:0] in_3,
  output [7:0] ARegister,
  output [2:0] Status
);

  wire and_1_out, clock_1_out;
  wire [2:0] add_sub_8bits_1_zero_neg_over, multiplexer_2_out;
  wire [2:2] mult_1_inputtoolarge;
  wire [7:0] add_sub_8bits_1_r, demultiplexer_1_out0, demultiplexer_1_out1, demultiplexer_2_out0,
       demultiplexer_2_out1, LR_out1, mult_1_out_4, multiplexer_1_out, RR_out1;

  Clock clock_1 (.out(clock_1_out));
  and and_1 (and_1_out, clock_1_out, Enable_Mult_AddSub[2]);
  Register8Bit RR (.in1(in_3), .out1(RR_out1), .Enbl(and_1_out));
  Register8Bit LR (.in1(in_2), .out1(LR_out1), .Enbl(and_1_out));
  Demultiplexer #(.width(8), .enable("false")) demultiplexer_1 (
    .out0(demultiplexer_1_out0), .out1(demultiplexer_1_out1), .in(RR_out1), .sel(Enable_Mult_AddSub[1]));
  Demultiplexer #(.width(8), .enable("false")) demultiplexer_2 (
    .out0(demultiplexer_2_out0), .out1(demultiplexer_2_out1), .in(LR_out1), .sel(Enable_Mult_AddSub[1]));
  Mult mult_1 (
    .B(demultiplexer_1_out1), .A(demultiplexer_2_out1), .inputTooLarge(mult_1_inputtoolarge[2]),
    .out_4(mult_1_out_4));
  Add_Sub_8Bits add_sub_8bits_1 (
    .A(demultiplexer_1_out0), .B(demultiplexer_2_out0), .Add_Sub(Enable_Mult_AddSub[0]),
    .Zero_Neg_Over(add_sub_8bits_1_zero_neg_over), .R(add_sub_8bits_1_r));
  Multiplexer #(.width(8), .enable("false")) multiplexer_1 (
    .in0(add_sub_8bits_1_r), .in1(mult_1_out_4), .out(multiplexer_1_out), .sel(Enable_Mult_AddSub[1]));
  Multiplexer #(.width(3), .enable("false")) multiplexer_2 (
    .in0(add_sub_8bits_1_zero_neg_over), .in1({3{mult_1_inputtoolarge[2]}}), .out(multiplexer_2_out),
    .sel(Enable_Mult_AddSub[1]));
  Register8Bit register8bit_1 (.in1(multiplexer_1_out), .out1(ARegister), .Enbl(and_1_out));
  Register3Bit register3bit_1 (.in1(multiplexer_2_out), .in_2(and_1_out), .out1(Status));
endmodule

module numeric_keypad (
  input  D0,
  input  D1,
  input  D2,
  input  D3,
  input  D4,
  input  D5,
  input  D6,
  input  D7,
  input  D8,
  input  D9,
  output [7:0] out_11
);

  wire or_1_out, or_2_out, or_3_out, or_4_out, or_5_out;

  or or_1 (or_1_out, D9, D8, D7, D6, D5, D4, D3, D2, D1, D0);
  or or_2 (or_2_out, D8, D9);
  or or_3 (or_3_out, D4, D5, D6, D7);
  or or_4 (or_4_out, D6, D3, D2, D7);
  or or_5 (or_5_out, D9, D7, D5, D3, D1);
  D_Flip_Flop d_ff_1 (.D(or_2_out), .clk(or_1_out), .Q(out_11[3]));  // open: Qn, preset, reset
  D_Flip_Flop d_ff_2 (.D(or_3_out), .clk(or_1_out), .Q(out_11[2]));  // open: Qn, preset, reset
  D_Flip_Flop d_ff_3 (.D(or_4_out), .clk(or_1_out), .Q(out_11[1]));  // open: Qn, preset, reset
  D_Flip_Flop d_ff_4 (.D(or_5_out), .clk(or_1_out), .Q(out_11[0]));  // open: Qn, preset, reset

  assign out_11[7:4] = 4'b0000;
endmodule

module Add_1Bits (
  input  A,
  input  B,
  input  Cin,
  output Sum,
  output Cout
);

  wire and_1_out, and_2_out, xor_1_out;

  xor xor_1 (xor_1_out, A, B);
  and and_1 (and_1_out, xor_1_out, Cin);
  and and_2 (and_2_out, A, B);
  xor xor_2 (Sum, xor_1_out, Cin);
  or or_1 (Cout, and_1_out, and_2_out);
endmodule

module MAR (
  input  Clk,
  input  [3:0] DataInput,
  input  Write,
  output [3:0] DataOutput
);

  four_bit_storage four_bit_storage_1 (.Out1(DataOutput), .Write(Write), .Clock(Clk), .In1(DataInput));
endmodule

module PC_incr (
  input  StopIn,
  input  [3:0] Counter,
  input  [3:0] PCIn,
  output [3:0] PCOut
);

  wire not_1_out, true_four_compare_1_out_3;
  wire [3:0] and_1_out;

  not not_1 (not_1_out, StopIn);
  and and_1 (and_1_out[0], not_1_out, true_four_compare_1_out_3);
  true_four_compare true_four_compare_1 (.out_3(true_four_compare_1_out_3), .in_2(4'b1000), .in_1(Counter));
  Add_4bit add_4bit_1 (.B(and_1_out), .A(PCIn), .Sum(PCOut));  // open: CIN, out_5
endmodule

module Register8Bit (
  input  [7:0] in1,
  input  Enbl,
  output [7:0] out1
);

  D_Flip_Flop d_ff_1 (.D(in1[0]), .clk(Enbl), .Q(out1[0]));  // open: Qn, preset, reset
  D_Flip_Flop d_ff_2 (.D(in1[1]), .clk(Enbl), .Q(out1[1]));  // open: Qn, preset, reset
  D_Flip_Flop d_ff_3 (.D(in1[2]), .clk(Enbl), .Q(out1[2]));  // open: Qn, preset, reset
  D_Flip_Flop d_ff_4 (.D(in1[3]), .clk(Enbl), .Q(out1[3]));  // open: Qn, preset, reset
  D_Flip_Flop d_ff_5 (.D(in1[4]), .clk(Enbl), .Q(out1[4]));  // open: Qn, preset, reset
  D_Flip_Flop d_ff_6 (.D(in1[5]), .clk(Enbl), .Q(out1[5]));  // open: Qn, preset, reset
  D_Flip_Flop d_ff_7 (.D(in1[6]), .clk(Enbl), .Q(out1[6]));  // open: Qn, preset, reset
  D_Flip_Flop d_ff_8 (.D(in1[7]), .clk(Enbl), .Q(out1[7]));  // open: Qn, preset, reset
endmodule

module Register3Bit (
  input  [2:0] in1,
  input  in_2,
  output [2:0] out1
);

  D_Flip_Flop d_ff_1 (.D(in1[0]), .clk(in_2), .Q(out1[0]));  // open: Qn, preset, reset
  D_Flip_Flop d_ff_2 (.D(in1[1]), .clk(in_2), .Q(out1[1]));  // open: Qn, preset, reset
  D_Flip_Flop d_ff_3 (.D(in1[2]), .clk(in_2), .Q(out1[2]));  // open: Qn, preset, reset
endmodule

module sysBus (
  input  [7:0] in_1,
  input  [7:0] in_2,
  input  in_3,
  output [7:0] out_4
);

  Multiplexer #(.width(8), .enable("false")) multiplexer_1 (.in0(in_1), .in1(in_2), .out(out_4), .sel(in_3));
endmodule

module Add_4bit (
  input  [3:0] B,
  input  [3:0] A,
  input  CIN,
  output [3:0] Sum,
  output out_5
);

  wire add_1bits_1_cout, add_1bits_2_cout, add_1bits_3_cout;

  Add_1Bits add_1bits_1 (.A(A[0]), .B(B[0]), .Cin(CIN), .Sum(Sum[0]), .Cout(add_1bits_1_cout));
  Add_1Bits add_1bits_2 (.A(A[1]), .B(B[1]), .Cin(add_1bits_1_cout), .Sum(Sum[1]), .Cout(add_1bits_2_cout));
  Add_1Bits add_1bits_3 (.A(A[2]), .B(B[2]), .Cin(add_1bits_2_cout), .Sum(Sum[2]), .Cout(add_1bits_3_cout));
  Add_1Bits add_1bits_4 (.A(A[3]), .B(B[3]), .Cin(add_1bits_3_cout), .Sum(Sum[3]), .Cout(out_5));
endmodule

module Mult (
  input  [7:0] B,
  input  [7:0] A,
  output inputTooLarge,
  output [7:0] out_4
);

  wire or_1_out, or_3_out;
  wire [2:0] and_6_out, and_14_out;
  wire [3:0] add_4bit_1_sum, add_4bit_2_sum, and_4_out, and_11_out;
  wire [5:0] and_8_out;

  or or_1 (or_1_out, A[7], A[6], A[5], A[4]);
  or or_2 (inputTooLarge, or_1_out, or_3_out);
  and and_1 (and_4_out[3], A[3], B[3]);
  and and_2 (and_4_out[2], A[3], B[2]);
  or or_3 (or_3_out, B[4], B[5], B[6], B[7]);
  and and_3 (and_4_out[1], A[3], B[1]);
  and and_4 (and_4_out[0], A[3], B[0]);
  and and_5 (and_6_out[2], A[2], B[3]);
  Add_4bit add_4bit_1 (.B({1'b0, and_6_out}), .A(and_4_out), .CIN(1'b0), .Sum(add_4bit_1_sum), .out_5(and_8_out[5]));
  and and_6 (and_6_out[0], A[2], B[1]);
  and and_7 (and_6_out[1], A[2], B[2]);
  and and_8 (and_8_out[0], A[2], B[0]);
  and and_9 (and_11_out[3], A[1], B[3]);
  and and_10 (and_11_out[2], A[1], B[2]);
  Add_6bit add_6bit_1 (
    .B({2'b00, add_4bit_2_sum}), .A({and_8_out[5], add_4bit_1_sum, and_8_out[0]}), .CIN(1'b0),
    .SUM(out_4[7:2]));  // open: COUT
  and and_11 (and_11_out[0], A[1], B[0]);
  and and_12 (and_11_out[1], A[1], B[1]);
  and and_13 (and_14_out[2], A[0], B[3]);
  Add_4bit add_4bit_2 (
    .B({1'b0, and_14_out}), .A(and_11_out), .CIN(1'b0), .Sum({add_4bit_2_sum[2:0], out_4[1]}),
    .out_5(add_4bit_2_sum[3]));
  and and_14 (and_14_out[0], A[0], B[1]);
  and and_15 (and_14_out[1], A[0], B[2]);
  and and_16 (out_4[0], A[0], B[0]);
endmodule

module Add_6bit (
  input  [5:0] B,
  input  [5:0] A,
  input  CIN,
  output [5:0] SUM,
  output COUT
);

  wire add_1bits_1_cout, add_1bits_2_cout, add_1bits_3_cout, add_1bits_4_cout, add_1bits_5_cout;

  Add_1Bits add_1bits_1 (.A(A[0]), .B(B[0]), .Cin(CIN), .Sum(SUM[0]), .Cout(add_1bits_1_cout));
  Add_1Bits add_1bits_2 (.A(A[1]), .B(B[1]), .Cin(add_1bits_1_cout), .Sum(SUM[1]), .Cout(add_1bits_2_cout));
  Add_1Bits add_1bits_3 (.A(A[2]), .B(B[2]), .Cin(add_1bits_2_cout), .Sum(SUM[2]), .Cout(add_1bits_3_cout));
  Add_1Bits add_1bits_4 (.A(A[3]), .B(B[3]), .Cin(add_1bits_3_cout), .Sum(SUM[3]), .Cout(add_1bits_4_cout));
  Add_1Bits add_1bits_5 (.A(A[4]), .B(B[4]), .Cin(add_1bits_4_cout), .Sum(SUM[4]), .Cout(add_1bits_5_cout));
  Add_1Bits add_1bits_6 (.A(A[5]), .B(B[5]), .Cin(add_1bits_5_cout), .Sum(SUM[5]), .Cout(COUT));
endmodule

module delay_pc (
  input  Clk,
  input  Reset,
  output out_3
);

  wire delay_base_1_p3, delay_base_1_p4, delay_base_1_p5;

  // delay_base delay_base_1: pin names not known; wires that end beside it: Clk, Reset, delay_base_1_p3, delay_base_1_p4, delay_base_1_p5
  and and_1 (out_3, ~delay_base_1_p3, delay_base_1_p4, delay_base_1_p5);  // AND_Gate

  // Notes on the sheet:
  //   For incrementer, adds one to PC on second tick every 8 ticks
endmodule

module delay_base (
  input  Clk,
  input  Reset,
  output [3:0] out_3
);

  wire j_k_ff_1_q, j_k_ff_2_q, j_k_ff_3_q, j_k_ff_4_q, not_1_out, or_1_out, or_2_out, or_3_out, or_4_out;

  not not_1 (not_1_out, Reset);
  J_K_Flip_Flop j_k_ff_1 (.J(not_1_out), .K(1'b1), .clk(or_1_out), .Q(j_k_ff_1_q));  // open: Qn, preset, reset
  or or_1 (or_1_out, Clk, Reset);
  J_K_Flip_Flop j_k_ff_2 (.J(not_1_out), .K(1'b1), .clk(or_2_out), .Q(j_k_ff_2_q));  // open: Qn, preset, reset
  or or_2 (or_2_out, j_k_ff_1_q, Reset);
  or or_3 (or_3_out, j_k_ff_2_q, Reset);
  J_K_Flip_Flop j_k_ff_3 (.J(not_1_out), .K(1'b1), .clk(or_3_out), .Q(j_k_ff_3_q));  // open: Qn, preset, reset
  or or_4 (or_4_out, j_k_ff_3_q, Reset);
  J_K_Flip_Flop j_k_ff_4 (.J(not_1_out), .K(1'b1), .clk(or_4_out), .Q(j_k_ff_4_q));  // open: Qn, preset, reset
  Twos_Comp twos_comp_1 (
    .Enable(1'b1), .A(j_k_ff_1_q), .B(j_k_ff_2_q), .C(j_k_ff_3_q), .D(j_k_ff_4_q), .Aout(out_3[0]),
    .Bout(out_3[1]), .Cout(out_3[2]), .Dout(out_3[3]));  // open: in_6, in_7, in_8, in_9, out_14, out_15, out_16, out_17, Overflow
  // Probe on out_3
endmodule

module ROM_bonus (
  output [7:0] out_1,
  output [7:0] out_2,
  output [7:0] out_3,
  output [7:0] out_4,
  output [7:0] out_5,
  output [7:0] out_6,
  output [7:0] out_7,
  output [7:0] out_8,
  output [7:0] out_9,
  output [7:0] out_10,
  output [7:0] out_11,
  output [7:0] out_12,
  output [7:0] out_13,
  output [7:0] out_14,
  output [7:0] out_15,
  output [7:0] out_16
);


  assign out_1 = 8'h65;
  assign out_2 = 8'h74;
  assign out_3 = 8'he0;
  assign out_4 = {8{1'b0}};
  assign out_5 = 8'h7;
  assign out_6 = 8'h3;
  assign out_7 = 8'h1;
  assign out_8 = 8'h63;
  assign out_9 = 8'h74;
  assign out_10 = 8'h30;
  assign out_11 = 8'ha0;
  assign out_12 = 8'h83;
  assign out_13 = 8'h65;
  assign out_14 = 8'h76;
  assign out_15 = 8'h30;
  assign out_16 = 8'h85;
endmodule

module Three_Compare (
  input  [7:0] in_1,
  input  [2:0] in_2,
  output out_3
);

  wire xnor_1_out, xnor_2_out, xnor_3_out;

  xnor xnor_1 (xnor_1_out, in_1[5], in_2[0]);
  xnor xnor_2 (xnor_2_out, in_1[6], in_2[1]);
  xnor xnor_3 (xnor_3_out, in_1[7], in_2[2]);
  and and_1 (out_3, xnor_1_out, xnor_2_out, xnor_3_out);
endmodule

module pre_bus (
  input  [3:0] PC,
  input  [7:0] RAM,
  input  [7:0] CPU,
  input  [7:0] Keypad,
  input  [3:0] Count,
  output [7:0] out_6
);

  wire [3:0] undriven;

  Multiplexer #(.select(4), .width(8), .enable("false")) multiplexer_1 (
    .in1({undriven, PC}), .in3(RAM), .in5(Keypad), .in7(CPU), .in9(RAM), .in11(CPU), .in13(CPU), .out(out_6),
    .sel(Count));  // open: in0, in2, in4, in6, in8, in10, in12, in14, in15

  // Notes on the sheet:
  //   get from pc, get data from ram, send addr to ram, get result again, send new data for that addr, get data from input, send should display or should stop, send from cpu to display
endmodule

module post_bus (
  input  [7:0] in_1,
  input  [2:0] Count,
  output [7:0] RAM,
  output [7:0] CPU,
  output [7:0] Display
);

  Demultiplexer #(.select(3), .width(8), .tristate("true"), .enable("false")) demultiplexer_1 (
    .out1(Display), .out2(CPU), .out3(CPU), .out4(Display), .out5(CPU), .out6(Display), .out7(Display),
    .in(in_1), .sel(Count));  // open: out0

  assign RAM = Display;

  // Notes on the sheet:
  //   On last tick, check of opcode is for display
endmodule

module true_four_compare (
  input  [3:0] in_1,
  input  [3:0] in_2,
  output out_3
);

  wire xnor_1_out, xnor_2_out, xnor_3_out, xnor_4_out;

  xnor xnor_1 (xnor_1_out, in_1[0], in_2[0]);
  xnor xnor_2 (xnor_2_out, in_1[1], in_2[1]);
  xnor xnor_3 (xnor_3_out, in_1[2], in_2[2]);
  xnor xnor_4 (xnor_4_out, in_1[3], in_2[3]);
  and and_1 (out_3, xnor_1_out, xnor_2_out, xnor_3_out, xnor_4_out);
endmodule

module RW (
  input  [7:0] in_1,
  input  [3:0] in_2,
  output WriteTrigger,
  output out_4
);

  wire and_1_out, clock_1_out, true_four_compare_1_out_3, true_four_compare_2_out_3;

  Clock clock_1 (.out(clock_1_out));
  true_four_compare true_four_compare_1 (.out_3(true_four_compare_1_out_3), .in_2(4'b0111), .in_1(in_2));
  true_four_compare true_four_compare_2 (.out_3(true_four_compare_2_out_3), .in_2(4'b1011), .in_1(in_2));
  D_Flip_Flop d_ff_1 (.D(in_1[7]), .clk(and_1_out), .Q(WriteTrigger));  // open: Qn, preset, reset
  and and_1 (and_1_out, clock_1_out, true_four_compare_1_out_3);
  and and_2 (out_4, WriteTrigger, true_four_compare_2_out_3);
endmodule

module RAMaddrCount (
  input  [3:0] in_1,
  output out_2
);

  wire true_four_compare_1_out_3, true_four_compare_2_out_3;

  true_four_compare true_four_compare_1 (.out_3(true_four_compare_1_out_3), .in_2(4'b0001), .in_1(in_1));
  true_four_compare true_four_compare_2 (.out_3(true_four_compare_2_out_3), .in_2(4'b0111), .in_1(in_1));
  or or_1 (out_2, true_four_compare_1_out_3, true_four_compare_2_out_3);
endmodule

module ShouldDisplay (
  input  [7:0] in_1,
  input  [3:0] in_2,
  output out_3,
  output out_4
);

  wire and_1_out, clock_1_out, true_four_compare_1_out_3, true_four_compare_2_out_3;

  Clock clock_1 (.out(clock_1_out));
  true_four_compare true_four_compare_1 (.out_3(true_four_compare_1_out_3), .in_2(4'b0111), .in_1(in_2));
  true_four_compare true_four_compare_2 (.out_3(true_four_compare_2_out_3), .in_2(4'b1101), .in_1(in_2));
  D_Flip_Flop d_ff_1 (.D(in_1[6]), .clk(and_1_out), .Q(out_3));  // open: Qn, preset, reset
  and and_1 (and_1_out, clock_1_out, true_four_compare_1_out_3);
  and and_2 (out_4, out_3, true_four_compare_2_out_3);
endmodule

module pre_pc (
  input  [3:0] in_1,
  input  [3:0] in_2,
  input  [3:0] in_3
);
endmodule

module ROM_Mult (
  output [7:0] out_1,
  output [7:0] out_2,
  output [7:0] out_3,
  output [7:0] out_4,
  output [7:0] out_5,
  output [7:0] out_6,
  output [7:0] out_7,
  output [7:0] out_8,
  output [7:0] out_9,
  output [7:0] out_10,
  output [7:0] out_11,
  output [7:0] out_12,
  output [7:0] out_13,
  output [7:0] out_14,
  output [7:0] out_15,
  output [7:0] out_16
);


  assign out_1 = 8'hd0;
  assign out_2 = 8'h57;
  assign out_3 = {8{1'b0}};
  assign out_4 = {8{1'b0}};
  assign out_5 = 8'h7;
  assign out_6 = {8{1'b0}};
  assign out_7 = 8'h1;
  assign out_8 = 8'h63;
  assign out_9 = 8'h74;
  assign out_10 = 8'h30;
  assign out_11 = 8'ha0;
  assign out_12 = 8'h83;
  assign out_13 = 8'h65;
  assign out_14 = 8'h76;
  assign out_15 = 8'h30;
  assign out_16 = 8'h85;
endmodule
