// Logisim project CU.circ as structural Verilog: 1 circuit, main circuit CU
module CU (
  input  [7:0] Instruction,
  input  [7:0] MBR,
  input  [2:0] Counter,
  input  RegEqual,
  input  [7:0] Aout,
  input  [2:0] ALUstatus,
  output [3:0] Address,
  output WhichRegister,
  output Stop,
  output ALUOp,
  output WriteRegister,
  output Prt,
  output Inp,
  output [7:0] Data,
  output WriteInstruction,
  output [7:0] DataToReg,
  output BranchAddr
);

  wire and_1_out, and_2_out, and_3_out, and_4_out, and_6_out, decoder_1_out1, decoder_1_out2, decoder_1_out3,
       decoder_1_out4, decoder_1_out5, decoder_1_out6, decoder_1_out7, decoder_1_out8, decoder_1_out9,
       decoder_1_out10, decoder_1_out11, decoder_1_out12, decoder_1_out13, decoder_2_out0, decoder_2_out4,
       decoder_2_out6, decoder_2_out7, or_5_out, or_7_out;
  wire [7:0] multiplexer_1_out;
  wire [7:4] or_1_out;

  Decoder #(.select(4), .enable("false")) decoder_1 (
    .out0(Stop), .out1(decoder_1_out1), .out2(decoder_1_out2), .out3(decoder_1_out3), .out4(decoder_1_out4),
    .out5(decoder_1_out5), .out6(decoder_1_out6), .out7(decoder_1_out7), .out8(decoder_1_out8),
    .out9(decoder_1_out9), .out10(decoder_1_out10), .out11(decoder_1_out11), .out12(decoder_1_out12),
    .out13(decoder_1_out13), .sel(Instruction[7:4]));  // open: out14, out15
  Decoder #(.select(3), .enable("false")) decoder_2 (
    .out0(decoder_2_out0), .out1(WriteInstruction), .out4(decoder_2_out4), .out6(decoder_2_out6),
    .out7(decoder_2_out7), .sel(Counter));  // open: out2, out3, out5
  or or_1 (or_1_out[4], ALUstatus[0], ALUstatus[1]);
  or or_2 (Inp, decoder_1_out13, decoder_1_out12);
  and and_1 (and_1_out, decoder_2_out0, RegEqual);
  or or_3 (or_1_out[7], decoder_1_out9, decoder_1_out8);
  or or_4 (Prt, decoder_1_out11, decoder_1_out10);
  and and_2 (and_2_out, decoder_1_out4, and_1_out);
  and and_3 (and_3_out, ~and_1_out, decoder_1_out5);  // AND_Gate
  or or_5 (or_5_out, decoder_1_out7, decoder_1_out6);
  Multiplexer #(.width(8), .enable("false")) multiplexer_1 (
    .in0(MBR), .in1({or_1_out[7], Prt, Stop, or_1_out[4], Instruction[3:0]}), .out(multiplexer_1_out),
    .sel(decoder_2_out4));
  or or_6 (BranchAddr, and_2_out, and_3_out);
  and and_4 (and_4_out, or_5_out, decoder_2_out6);
  Multiplexer #(.width(8), .enable("false")) multiplexer_2 (
    .in0(multiplexer_1_out), .out(Data), .sel(decoder_2_out6));  // open: in1
  // Probe on {or_1_out[7], Prt, Stop, or_1_out[4], Instruction[3:0]}
  or or_7 (or_7_out, decoder_1_out2, decoder_1_out3);
  and and_5 (ALUOp, or_7_out, decoder_2_out7);
  and and_6 (and_6_out, or_7_out, decoder_2_out0);
  or or_8 (WriteRegister, and_6_out, and_4_out);
  Multiplexer #(.width(8), .enable("false")) multiplexer_3 (.in0(Aout), .in1(MBR), .out(DataToReg), .sel(and_4_out));

  assign Address = Instruction[3:0];
  assign WhichRegister = Instruction[4];

  // Notes on the sheet:
  //   Zero_Neg_Over
  //   Ld
  //   Str
  //   Sub
  //   Beq
  //   Bnq
  //   Add
  //   Special Data for Step 4
endmodule
